// Digital circuit Acc8-seq.dig as structural Verilog
module Acc8_seq (
  input  rst,
  input  clk,
  input  EN,
  output [7:0] R,
  output ovf
);

  wire [3:0] counter_1_out;
  wire [7:0] rom_1_d;

  Counter #(.Bits(4)) counter_1 (.en(EN), .C(clk), .clr(rst), .out(counter_1_out));  // open: ovf
  ROM #(.AddrBits(4), .Bits(8)) rom_1 (.A(counter_1_out), .sel(EN), .D(rom_1_d));
  Acc8 acc8_1 (.A(rom_1_d), .en(EN), .clk(clk), .rst(rst), .R(R), .ovf(ovf));

  // Notes on the sheet:
  //   contents of rom_1 (hex, n*v repeats v):
  //   4f,4,6,4f,9,5,6,7,8,9,10,11,12,13,14,15
endmodule
