// Digital circuit Acc8.dig as structural Verilog
module Acc8 (
  input  [7:0] A,
  input  en,
  input  clk,
  input  rst,
  output [7:0] R,
  output ovf
);

  wire and_1_out;
  wire [7:0] addsub8_ofv_1_s;

  and and_1 (and_1_out, en, ~ovf);  // And
  AddSub8_ofv addsub8_ofv_1 (.AS(rst), .B(R), .A(A), .S(addsub8_ofv_1_s), .OVF(ovf));
  // Reg8 reg8_1: pin names not known; wires that end beside it: clk, addsub8_ofv_1_s, rst, and_1_out, R
endmodule
