// Digital circuit Add8.dig as structural Verilog
module Add8 (
  input  A0,
  input  B0,
  input  Ci,
  input  A1,
  input  B1,
  input  A2,
  input  B2,
  input  A3,
  input  B3,
  input  A4,
  input  B4,
  input  A5,
  input  B5,
  input  A6,
  input  B6,
  input  A7,
  input  B7,
  output S0,
  output S1,
  output S2,
  output S3,
  output S4,
  output S5,
  output S6,
  output S7
);

  wire fa_2_co, fa_3_co, fa_4_co, fa_5_co, fa_6_co, fa_7_co, fa_8_co;

  FA fa_1 (.A(A7), .B(B7), .C1(fa_2_co), .S(S7));  // open: Co
  FA fa_2 (.A(A6), .B(B6), .C1(fa_3_co), .Co(fa_2_co), .S(S6));
  FA fa_3 (.A(A5), .B(B5), .C1(fa_4_co), .Co(fa_3_co), .S(S5));
  FA fa_4 (.A(A4), .B(B4), .C1(fa_5_co), .Co(fa_4_co), .S(S4));
  FA fa_5 (.A(A3), .B(B3), .C1(fa_6_co), .Co(fa_5_co), .S(S3));
  FA fa_6 (.A(A2), .B(B2), .C1(fa_7_co), .Co(fa_6_co), .S(S2));
  FA fa_7 (.A(A1), .B(B1), .C1(fa_8_co), .Co(fa_7_co), .S(S1));
  FA fa_8 (.A(A0), .B(B0), .C1(Ci), .Co(fa_8_co), .S(S0));
endmodule
