// Digital circuit AddSub8-ofv.dig as structural Verilog
module AddSub8_ofv (
  input  AS,
  input  [7:0] B,
  input  [7:0] A,
  output [7:0] S,
  output OVF
);

  AddSub8 addsub8_1 (.AS(AS), .B(B), .A(A), .S(S));
  // det_OVF det_ovf_1: pin names not known; wires that end beside it: AS, A[7], B[7], S[7], OVF
endmodule
