// Digital circuit AddSub8.dig as structural Verilog
module AddSub8 (
  input  AS,
  input  [7:0] B,
  input  [7:0] A,
  output [7:0] S
);

  wire [7:0] xor_1_out;

  assign xor_1_out = B ^ {8{AS}};  // XOr xor_1, 8 bits wide
  Add8 add8_1 (
    .A0(A[0]), .B0(xor_1_out[0]), .Ci(AS), .A1(A[1]), .B1(xor_1_out[1]), .A2(A[2]), .B2(xor_1_out[2]),
    .A3(A[3]), .B3(xor_1_out[3]), .A4(A[4]), .B4(xor_1_out[4]), .A5(A[5]), .B5(xor_1_out[5]), .A6(A[6]),
    .B6(xor_1_out[6]), .A7(A[7]), .B7(xor_1_out[7]), .S0(S[0]), .S1(S[1]), .S2(S[2]), .S3(S[3]), .S4(S[4]),
    .S5(S[5]), .S6(S[6]), .S7(S[7]));
endmodule
